# Fritzing sketch Dead Parrot Protocol (saved by Fritzing 1.0.6)
breadboards: 1

parts:
  A1 = Raspberry Pi Pico2
  S1 = Pushbutton [package="[SMD]"]
  S2 = Pushbutton [package="[SMD]"]
  PASSIVE_Buzzer = Piezo Buzzer
  D1 = LED_BARGRAPH_10 [package=led_bargaph_10]
  LED1 = RGB LED (com. cathode, rgb) [color="Red (633nm)" current=0.030A package="5 mm [THT]"]
  LED2 = smd LED [color="Red (633nm)" package="0603 [SMD]"]
  R1 = Resistor [tolerance=±5% power=0.25W resistance=220 package=THT]
  R2 = Resistor [tolerance=±5% power=0.25W resistance=220 package=THT]
  R3 = Resistor [tolerance=±5% power=0.25W resistance=220 package=THT]
  R4 = Resistor [tolerance=±5% power=0.25W resistance=220 package=THT]
  R5 = Resistor [tolerance=±5% power=0.25W resistance=220 package=THT]
  R7 = Resistor [tolerance=±5% power=0.25W resistance=220 package=THT]
  R8 = Resistor [tolerance=±5% power=0.25W resistance=220 package=THT]
  R9 = Resistor [tolerance=±5% power=0.25W resistance=220 package=THT]
  R10 = Resistor [tolerance=±5% power=0.25W resistance=220 package=THT]
  R13 = Resistor [tolerance=±5% power=0.25W resistance=220 package=THT]
  U1 = POT [knob_status=50% power=0.5W package=pot_alpha_rv16af-20]
  R14 = Resistor [tolerance=±5% power=0.25W resistance=220 package=THT]
  ACTIVE_Buzzer = Piezo Buzzer
  R15 = Resistor [tolerance=±5% power=0.25W resistance=220 package=THT]

nets:
  N1: A1.pin_1, D1.A_A
  N2: A1.pin_2, D1.B_A
  N3: A1.pin_3, A1.pin_8, A1.pin_13, A1.pin_18, A1.pin_23, A1.pin_28, A1.pin_33, A1.pin_38, A1.pin_42, S1.Pin_1, S1.Pin_2, S2.Pin_1, S2.Pin_2, PASSIVE_Buzzer.pin_2, R1.Pin_0, R2.Pin_0, R3.Pin_0, R4.Pin_0, R5.Pin_0, R7.Pin_0, R8.Pin_0, R9.Pin_0, R10.Pin_0, R13.Pin_0, U1.A, R14.Pin_1
  N4: A1.pin_4, D1.C_A
  N5: A1.pin_5, D1.D_A
  N6: A1.pin_6, D1.E_A
  N7: A1.pin_7, D1.F_A
  N8: A1.pin_9, D1.G_A
  N9: A1.pin_10, D1.H_A
  N10: A1.pin_11, D1.I_A
  N11: A1.pin_12, ACTIVE_Buzzer.pin_1
  N12: A1.pin_14, D1.J_A
  N13: A1.pin_17, LED2.cathode
  N14: A1.pin_19, S2.Pin_3, S2.Pin_4
  N15: A1.pin_20, S1.Pin_3, S1.Pin_4
  N16: A1.pin_21, PASSIVE_Buzzer.pin_1
  N17: A1.pin_24, LED1.blue_anode
  N18: A1.pin_25, LED1.common_cathode
  N19: A1.pin_26, LED1.red_anode
  N20: A1.pin_31, U1.S
  N21: A1.pin_36, U1.E, R15.Pin_0
  N22: D1.J_C, R1.Pin_1
  N23: D1.I_C, R2.Pin_1
  N24: D1.H_C, R3.Pin_1
  N25: D1.G_C, R4.Pin_1
  N26: D1.F_C, R5.Pin_1
  N27: D1.E_C, R7.Pin_1
  N28: D1.D_C, R8.Pin_1
  N29: D1.C_C, R9.Pin_1
  N30: D1.B_C, R10.Pin_1
  N31: D1.A_C, R13.Pin_1
  N32: LED1.green_anode, R15.Pin_1
  N33: LED2.anode, R14.Pin_0

custom parts:
  Raspberry Pi Pico2: Raspberry Pi Pico 2W is our new $7 microcontroller board, built on RP2350: our new high-performance, secure microcontroller with on board WiFi.
  Piezo Buzzer: Part from https://www.nutsvolts.com/magazine/article/november2012_SmileysWorkshop. Breadboard and icon images modified to be 0.3" in spacing and be more similar to the actual physical part.
